# Fritzing sketch PCB_design (saved by Fritzing 0.9.3b)
circuit board: 9.50095cm x 5.96566cm

parts:
  VCC1 = Battery
  S5 = Pushbutton [package="[SMD]"]
  S4 = Pushbutton [package="[SMD]"]
  S3 = Pushbutton [package="[SMD]"]
  S1 = Pushbutton [package="[SMD]"]
  S2 = Pushbutton [package="[SMD]"]
  S6 = Pushbutton [package="[SMD]"]
  R1 = Resistor [tolerance=±5% resistance=220 package="0603 [SMD]"]
  R2 = Resistor [tolerance=±5% resistance=220 package="0603 [SMD]"]
  R4 = Resistor [tolerance=±5% resistance=220 package="0603 [SMD]"]
  R3 = Resistor [tolerance=±5% resistance=220 package="0603 [SMD]"]
  LED2 = smd LED [color="Red (633nm)" package="0603 [SMD]"]
  LED3 = smd LED [color="Red (633nm)" package="0603 [SMD]"]
  LED4 = smd LED [color="Red (633nm)" package="0603 [SMD]"]
  LED5 = smd LED [color="Green (565nm)" package="0603 [SMD]"]
  ATtiny4313 = SOIC18-W [chip_label=ATtiny4313 package=SO(w)]  # not connected
  U2 = RJ45 Jack [package=rj45-8]
  U1 = RJ45 Jack [package=rj45-8]

nets:
  N1: VCC1.-, S5.Pin_3, S4.Pin_3, S4.Pin_4, S3.Pin_1, S3.Pin_2, S1.Pin_3, S2.Pin_3, S6.Pin_3, S6.Pin_4, R1.Pin_0, R4.Pin_1
  N2: S5.Pin_1, S5.Pin_2
  N3: S4.Pin_1, S4.Pin_2
  N4: S1.Pin_1, S1.Pin_2
  N5: S2.Pin_1, S2.Pin_2
  N6: S6.Pin_1, S6.Pin_2
  N7: R1.Pin_1, LED2.cathode, LED3.cathode, LED4.cathode
  N8: R2.Pin_0, U2.3
  N9: R4.Pin_0, LED5.cathode
  N10: R3.Pin_1, U1.3
